# Fritzing sketch Controlling SG90 with LDR and NodeMCU (saved by Fritzing 0.9.3b)
circuit board: 8.46667cm x 5.64444cm
breadboards: 1

parts:
  R1 = Photocell (LDR) [package=THT]
  J1 = Basic Servo
  U1 = NodeMCU V1.0
  R2 = Resistor [tolerance=±5% resistance=10k package="2512 [SMD]"]

nets:
  N1: R1.pin_0, U1.A0, R2.Pin_0
  GND: R1.pin_1, J1.gnd, U1.GND
  VCC: J1.vcc, U1.Vin, R2.Pin_1
  N2: J1.pulse, U1.D0

custom parts:
  NodeMCU V1.0: ESP8266 based NodeMCU
